// Logisim project Teclado.circ as structural Verilog
module Teclado (
  input  in_1,
  input  in_2,
  input  in_3,
  input  in_4,
  input  A,
  input  K,
  input  U,
  input  B,
  input  L,
  input  V,
  input  C,
  input  M,
  input  W,
  input  D,
  input  N,
  input  X,
  input  E,
  input  O,
  input  Y,
  input  F,
  input  P,
  input  Z,
  input  G,
  input  Q,
  input  H,
  input  R,
  input  I,
  input  S,
  input  J,
  input  T,
  output [24:0] out_31,
  output [24:0] out_32,
  output [3:0] out_33,
  output [24:0] out_34,
  output [24:0] out_35,
  output [24:0] out_36,
  output [24:0] out_37,
  output [24:0] out_38
);

  wire and_1_out, Clock, Enable, not_1_out;
  wire [3:0] EA, EC, ED, EE, EF, EG, EH;
  wire [24:0] Tecla;

  Clock clock_1 (.out(Clock));
  Define_Tecla define_tecla_1 (.in_2(1'b0), .in_3(A), .in_4(in_1), .in_1(25'hf94a4f), .out_5(Tecla));
  Define_Tecla define_tecla_2 (.in_2(1'b0), .in_3(B), .in_4(in_1), .in_1(25'haad6bf), .out_5(Tecla));
  Define_Tecla define_tecla_3 (.in_2(1'b0), .in_3(C), .in_4(in_1), .in_1(25'h118c63f), .out_5(Tecla));
  Define_Tecla define_tecla_4 (.in_2(1'b0), .in_3(D), .in_4(in_1), .in_1(25'he8c63f), .out_5(Tecla));
  Define_Tecla define_tecla_5 (.in_2(1'b0), .in_3(E), .in_4(in_1), .in_1(25'h15ad6bf), .out_5(Tecla));
  Define_Tecla define_tecla_6 (.in_2(1'b0), .in_3(F), .in_4(in_1), .in_1(25'h14a529f), .out_5(Tecla));
  Define_Tecla define_tecla_7 (.in_2(1'b0), .in_3(G), .in_4(in_1), .in_1(25'h16ad63f), .out_5(Tecla));
  Define_Tecla define_tecla_8 (.in_2(1'b0), .in_3(H), .in_4(in_1), .in_1(25'h1f2109f), .out_5(Tecla));
  Define_Tecla define_tecla_9 (.in_2(1'b0), .in_3(I), .in_4(in_1), .in_1(25'h5c00), .out_5(Tecla));
  Define_Tecla define_tecla_10 (.in_2(1'b0), .in_3(J), .in_4(in_1), .in_1(25'h1e08422), .out_5(Tecla));
  Define_Tecla define_tecla_11 (.in_2(1'b0), .in_3(K), .in_4(in_1), .in_1(25'h115109f), .out_5(Tecla));
  Define_Tecla define_tecla_12 (.in_2(1'b0), .in_3(L), .in_4(in_1), .in_1(25'h843f), .out_5(Tecla));
  Define_Tecla define_tecla_13 (.in_2(1'b0), .in_3(M), .in_4(in_1), .in_1(25'h1f4191f), .out_5(Tecla));
  Define_Tecla define_tecla_14 (.in_2(1'b0), .in_3(N), .in_4(in_1), .in_1(25'h1e0991f), .out_5(Tecla));
  Define_Tecla define_tecla_15 (.in_2(1'b0), .in_3(O), .in_4(in_1), .in_1(25'he8c62e), .out_5(Tecla));
  Define_Tecla define_tecla_16 (.in_2(1'b0), .in_3(P), .in_4(in_1), .in_1(25'hc94a5f), .out_5(Tecla));
  Define_Tecla define_tecla_17 (.in_2(1'b0), .in_3(Q), .in_4(in_1), .in_1(25'hd9562e), .out_5(Tecla));
  Define_Tecla define_tecla_18 (.in_2(1'b0), .in_3(R), .in_4(in_1), .in_1(25'hd94a5f), .out_5(Tecla));
  Define_Tecla define_tecla_19 (.in_2(1'b0), .in_3(S), .in_4(in_1), .in_1(25'h12ad6a9), .out_5(Tecla));
  Define_Tecla define_tecla_20 (.in_2(1'b0), .in_3(T), .in_4(in_1), .in_1(25'h1087e10), .out_5(Tecla));
  Define_Tecla define_tecla_21 (.in_2(1'b0), .in_3(U), .in_4(in_1), .in_1(25'h1e0843e), .out_5(Tecla));
  Define_Tecla define_tecla_22 (.in_2(1'b0), .in_3(V), .in_4(in_1), .in_1(25'h1c1045c), .out_5(Tecla));
  Define_Tecla define_tecla_23 (.in_2(1'b0), .in_3(W), .in_4(in_1), .in_1(25'h1f11c5f), .out_5(Tecla));
  Define_Tecla define_tecla_24 (.in_2(1'b0), .in_3(X), .in_4(in_1), .in_1(25'h1151151), .out_5(Tecla));
  Define_Tecla define_tecla_25 (.in_2(1'b0), .in_3(Y), .in_4(in_1), .in_1(25'h1041d10), .out_5(Tecla));
  Define_Tecla define_tecla_26 (.in_2(1'b0), .in_3(Z), .in_4(in_1), .in_1(25'h19ad6b3), .out_5(Tecla));
  // Probe on EC
  Counter #(.width(4), .max('hf)) counter_1 (.load(1'b1), .Q(EC), .clk(Clock));  // open: D, count, carry, clr
  // Probe on ED
  Counter #(.width(4), .max('hf)) counter_2 (.load(1'b1), .Q(ED), .clk(Clock));  // open: D, count, carry, clr
  // Probe on EE
  Counter #(.width(4), .max('hf)) counter_3 (.load(1'b1), .Q(EE), .clk(Clock));  // open: D, count, carry, clr
  // Probe on EF
  Counter #(.width(4), .max('hf)) counter_4 (.load(1'b1), .Q(EF), .clk(Clock));  // open: D, count, carry, clr
  // Probe on EG
  Counter #(.width(4), .max('hf)) counter_5 (.load(1'b1), .Q(EG), .clk(Clock));  // open: D, count, carry, clr
  // Probe on Tecla
  // Probe on EA
  or or_1 (Enable, A, B, C, D, E, F, G, H, J, K, L, M, N, O, P, Q, R, S, T, U, V, W, X, Y, Z);
  Registrador registrador_1 (
    .in_1(EA), .in_2(Tecla), .in_3(out_33), .C(Clock), .R(in_3), .E(Enable), .out_12(out_31),
    .out_13(out_32), .in_6(EC), .in_7(ED), .in_8(EF), .in_9(EG), .in_10(EH), .out_14(out_34),
    .out_15(out_35), .out_16(out_36), .out_17(out_37), .out_18(out_38));
  // Probe on out_33
  and and_1 (and_1_out, Clock, in_2);
  Counter #(.width(4), .max('hf)) counter_6 (.Q(EA), .clk(Enable), .clr(in_3));  // open: load, D, count, carry
  not not_1 (not_1_out, Enable);
  Multiplexer #(.width(25)) multiplexer_1 (.in0({25{1'b0}}), .out(Tecla), .sel(1'b0), .en(not_1_out));  // open: in1
  Counter #(.width(4), .max('hf)) counter_7 (.Q(out_33), .clk(and_1_out), .clr(in_4));  // open: load, D, count, carry
  DotMatrix #(.matrixrows(5)) dotmatrix_1 (
    .col0(out_32[4:0]), .col1(out_32[9:5]), .col2(out_32[14:10]), .col3(out_32[19:15]), .col4(out_32[24:20]));

  // Other names for the same wires on the sheet: EB[3:0] = out_33; ECO[24:0] = out_34; EDO[24:0] = out_35;
  //   EEO[24:0] = out_36; EFO[24:0] = out_37; EGO[24:0] = out_38; ET = in_1; R1 = A; R2 = B; R3 = C; R4 = D; R5 = E;
  //   R6 = F; R7 = G; R8 = H; R9 = I; R10 = J; R11 = K; R12 = L; R13 = M; R14 = N; R15 = O; R16 = P; R17 = Q; R18 = R;
  //   R19 = S; R20 = T; R21 = U; R22 = V; R23 = W; R24 = X; R25 = Y; R26 = Z; ResetCount = in_4; ResetLetras = in_3;
  //   Show = in_2
endmodule

module Define_Tecla (
  input  [24:0] in_1,
  input  in_2,
  input  in_3,
  input  in_4,
  output [24:0] out_5
);

  wire and_1_out;

  and and_1 (and_1_out, in_3, in_4);
  Multiplexer #(.width(25)) multiplexer_1 (.in0(in_1), .out(out_5), .sel(in_2), .en(and_1_out));  // open: in1
endmodule

module Registrador (
  input  [3:0] in_1,
  input  [24:0] in_2,
  input  [3:0] in_3,
  input  C,
  input  R,
  input  [3:0] in_6,
  input  [3:0] in_7,
  input  [3:0] in_8,
  input  [3:0] in_9,
  input  [3:0] in_10,
  input  E,
  output [24:0] out_12,
  output [24:0] out_13,
  output [24:0] out_14,
  output [24:0] out_15,
  output [24:0] out_16,
  output [24:0] out_17,
  output [24:0] out_18
);

  wire E1, E2, E3, E4, E5, E6, E7, E8, E9, E10, E11, E12, E13, E14, E15, E16, R1, R2, R3, R4, R5, R6, R7, R8,
       R9, R10, R11, R12, R13, R14, R15, R16;
  wire [3:0] ER;
  wire [24:0] DataR1, DataR2, DataR3, DataR4, DataR5, DataR6, DataR7, DataR8, DataR9, DataR10, DataR11,
       DataR12, DataR13, DataR14, DataR15, DataR16, R1O, R2O, R3O, R4O, R5O, R6O, R7O, R8O, R9O, R10O, R11O,
       R12O, R13O, R14O, R15O, R16O, R913;

  Demultiplexer #(.select(4)) demultiplexer_1 (
    .out0(E1), .out1(E2), .out2(E3), .out3(E4), .out4(E5), .out5(E6), .out6(E7), .out7(E8), .out8(E9),
    .out9(E10), .out10(E11), .out11(E12), .out12(E13), .out13(E14), .out14(E15), .out15(E16), .in(E),
    .sel(in_1));  // open: en
  Multiplexer #(.select(4), .width(25)) multiplexer_1 (
    .in0(R1O), .in1(R2O), .in2(R3O), .in3(R4O), .in4(R5O), .in5(R6O), .in6(R7O), .in7(R8O), .in8(R9O),
    .in9(R10O), .in10(R11O), .in11(R12O), .in12(R13O), .in13(R14O), .in14(R15O), .in15(R16O), .out(out_12),
    .sel(in_1));  // open: en
  Multiplexer #(.select(4), .width(25)) multiplexer_2 (
    .in0(R1O), .in1(R2O), .in2(R3O), .in3(R4O), .in4(R5O), .in5(R6O), .in6(R7O), .in7(R8O), .in8(R9O),
    .in9(R10O), .in10(R11O), .in11(R12O), .in12(R13O), .in13(R14O), .in14(R15O), .in15(R16O), .out(out_14),
    .sel(in_6));  // open: en
  Multiplexer #(.select(4), .width(25)) multiplexer_3 (
    .in0(R1O), .in1(R2O), .in2(R3O), .in3(R4O), .in4(R5O), .in5(R6O), .in6(R7O), .in7(R8O), .in8(R9O),
    .in9(R10O), .in10(R11O), .in11(R12O), .in12(R13O), .in13(R14O), .in14(R15O), .in15(R16O), .out(out_17),
    .sel(in_9));  // open: en
  Register #(.width(25)) register_1 (.D(DataR1), .en(E1), .Q(R1O), .clk(C), .clr(R));
  Register #(.width(25)) register_2 (.D(DataR5), .en(E5), .Q(R5O), .clk(C), .clr(R));
  Register #(.width(25)) register_3 (.D(DataR9), .en(E9), .Q(R9O), .clk(C), .clr(R));
  Register #(.width(25)) register_4 (.D(DataR13), .en(E13), .Q(R913), .clk(C), .clr(R));
  Register #(.width(25)) register_5 (.D(DataR2), .en(E2), .Q(R2O), .clk(C), .clr(R));
  Register #(.width(25)) register_6 (.D(DataR6), .en(E6), .Q(R6O), .clk(C), .clr(R));
  Register #(.width(25)) register_7 (.D(DataR10), .en(E10), .Q(R10O), .clk(C), .clr(R));
  Register #(.width(25)) register_8 (.D(DataR14), .en(E14), .Q(R14O), .clk(C), .clr(R));
  Demultiplexer #(.select(4)) demultiplexer_2 (
    .out0(R1), .out1(R2), .out2(R3), .out3(R4), .out4(R5), .out5(R6), .out6(R7), .out7(R8), .out8(R9),
    .out9(R10), .out10(R11), .out11(R12), .out12(R13), .out13(R14), .out14(R15), .out15(R16), .in(1'b1),
    .sel(ER), .en(R));
  Multiplexer #(.select(4), .width(25)) multiplexer_4 (
    .in0(R1O), .in1(R2O), .in2(R3O), .in3(R4O), .in4(R5O), .in5(R6O), .in6(R7O), .in7(R8O), .in8(R9O),
    .in9(R10O), .in10(R11O), .in11(R12O), .in12(R13O), .in13(R14O), .in14(R15O), .in15(R16O), .out(out_13),
    .sel(in_3));  // open: en
  Multiplexer #(.select(4), .width(25)) multiplexer_5 (
    .in0(R1O), .in1(R2O), .in2(R3O), .in3(R4O), .in4(R5O), .in5(R6O), .in6(R7O), .in7(R8O), .in8(R9O),
    .in9(R10O), .in10(R11O), .in11(R12O), .in12(R13O), .in13(R14O), .in14(R15O), .in15(R16O), .out(out_15),
    .sel(in_7));  // open: en
  Multiplexer #(.select(4), .width(25)) multiplexer_6 (
    .in0(R1O), .in1(R2O), .in2(R3O), .in3(R4O), .in4(R5O), .in5(R6O), .in6(R7O), .in7(R8O), .in8(R9O),
    .in9(R10O), .in10(R11O), .in11(R12O), .in12(R13O), .in13(R14O), .in14(R15O), .in15(R16O), .out(out_18),
    .sel(in_10));  // open: en
  Register #(.width(25)) register_9 (.D(DataR3), .en(E3), .Q(R3O), .clk(C), .clr(R));
  Register #(.width(25)) register_10 (.D(DataR7), .en(E7), .Q(R7O), .clk(C), .clr(R));
  Register #(.width(25)) register_11 (.D(DataR11), .en(E11), .Q(R11O), .clk(C), .clr(R));
  Register #(.width(25)) register_12 (.D(DataR15), .en(E15), .Q(R15O), .clk(C), .clr(R));
  Demultiplexer #(.select(4), .width(25)) demultiplexer_3 (
    .out0(DataR1), .out1(DataR2), .out2(DataR3), .out3(DataR4), .out4(DataR5), .out5(DataR6), .out6(DataR7),
    .out7(DataR8), .out8(DataR9), .out9(DataR10), .out10(DataR11), .out11(DataR12), .out12(DataR13),
    .out13(DataR14), .out14(DataR15), .out15(DataR16), .in(in_2), .sel(in_1));  // open: en
  Multiplexer #(.select(4), .width(25)) multiplexer_7 (
    .in0(R1O), .in1(R2O), .in2(R3O), .in3(R4O), .in4(R5O), .in5(R6O), .in6(R7O), .in7(R8O), .in8(R9O),
    .in9(R10O), .in10(R11O), .in11(R12O), .in12(R13O), .in13(R14O), .in14(R15O), .in15(R16O), .out(out_16),
    .sel(in_8));  // open: en
  Register #(.width(25)) register_13 (.D(DataR4), .en(E4), .Q(R4O), .clk(C), .clr(R));
  Register #(.width(25)) register_14 (.D(DataR8), .en(E8), .Q(R8O), .clk(C), .clr(R));
  Register #(.width(25)) register_15 (.D(DataR12), .en(E12), .Q(R12O), .clk(C), .clr(R));
  Register #(.width(25)) register_16 (.D(DataR16), .en(E16), .Q(R16O), .clk(C), .clr(R));

  // Other names for the same wires on the sheet: Data[24:0] = in_2; EA[3:0] = in_1; EB[3:0] = in_3; EC[3:0] = in_6;
  //   ED[3:0] = in_7; EE[3:0] = in_8; EF[3:0] = in_9; EG[3:0] = in_10
endmodule

module Teste (
  input  in_1,
  input  in_2
);

  wire A, B, C, CountR, D, E, F, G, H, I, interruptor_1_out_2, interruptor_1_out_3, interruptor_2_out_2,
       interruptor_2_out_3, interruptor_3_out_2, interruptor_3_out_3, interruptor_4_out_2,
       interruptor_4_out_3, J, K, KeyR, L, M, N, O, P, Q, R, S, T, teclado_1_p15, U, V, W, X, Y, Z;
  wire [3:0] PressedKeyPos;
  wire [24:0] ECO, EDO, EEO, EFO, EGO, LastKey, PressedKeys;

  Interruptor interruptor_1 (.in_1(in_1), .out_2(interruptor_1_out_2), .out_3(interruptor_1_out_3));
  Interruptor interruptor_2 (.in_1(in_2), .out_2(interruptor_2_out_2), .out_3(interruptor_2_out_3));
  Button button_1 (.out(CountR));
  Interruptor interruptor_3 (.in_1(CountR), .out_2(interruptor_3_out_2), .out_3(interruptor_3_out_3));
  Interruptor interruptor_4 (.in_1(KeyR), .out_2(interruptor_4_out_2), .out_3(interruptor_4_out_3));
  Button button_2 (.out(KeyR));
  // Teclado teclado_1: pin names not known; wires that end beside it: A, B, in_1, C, D, E, F, in_2, G, H, I, J, K, L, teclado_1_p15, M, N, O, P, Q, CountR, R, S, T, KeyR, U, V, W, X, Y, Z, LastKey, PressedKeys, PressedKeyPos, PressedKeys, PressedKeyPos
  LED led_1 (.in(interruptor_1_out_2));
  LED led_2 (.in(interruptor_1_out_3));
  LED led_3 (.in(interruptor_2_out_2));
  LED led_4 (.in(interruptor_2_out_3));
  LED led_5 (.in(interruptor_3_out_2));
  LED led_6 (.in(interruptor_3_out_3));
  LED led_7 (.in(interruptor_4_out_2));
  LED led_8 (.in(interruptor_4_out_3));
  Clock clock_1 (.out(teclado_1_p15));
  Button u_Q (.out(Q));
  Button u_A (.out(A));
  DotMatrix #(.matrixrows(5)) dotmatrix_1 (
    .col0(LastKey[4:0]), .col1(LastKey[9:5]), .col2(LastKey[14:10]), .col3(LastKey[19:15]),
    .col4(LastKey[24:20]));
  Button u_W (.out(W));
  Button u_R (.out(R));
  Button u_E (.out(E));
  Button u_D (.out(D));
  Button u_S (.out(S));
  Button u_C (.out(C));
  Button u_X (.out(X));
  Button u_Z (.out(Z));
  Button u_T (.out(T));
  Button u_Y (.out(Y));
  Button u_F (.out(F));
  Button u_H (.out(H));
  Button u_G (.out(G));
  Button u_N (.out(N));
  Button u_B (.out(B));
  Button u_V (.out(V));
  DotMatrix #(.matrixrows(5)) dotmatrix_2 (
    .col0(PressedKeys[4:0]), .col1(PressedKeys[9:5]), .col2(PressedKeys[14:10]), .col3(PressedKeys[19:15]),
    .col4(PressedKeys[24:20]));
  // Probe on PressedKeyPos
  Button u_I (.out(I));
  Button u_O (.out(O));
  Button u_U (.out(U));
  Button u_J (.out(J));
  Button u_K (.out(K));
  Button u_L (.out(L));
  Button u_M (.out(M));
  Button u_P (.out(P));
  DotMatrix #(.matrixcols(29), .matrixrows(5)) dotmatrix_3 (
    .col0(ECO[4:0]), .col1(ECO[9:5]), .col2(ECO[14:10]), .col3(ECO[19:15]), .col4(ECO[24:20]),
    .col5({5{1'b0}}), .col6(EDO[4:0]), .col7(EDO[9:5]), .col8(EDO[14:10]), .col9(EDO[19:15]),
    .col10(EDO[24:20]), .col11({5{1'b0}}), .col12(EEO[4:0]), .col13(EEO[9:5]), .col14(EEO[14:10]),
    .col15(EEO[19:15]), .col16(EEO[24:20]), .col17({5{1'b0}}), .col18(EFO[4:0]), .col19(EFO[9:5]),
    .col20(EFO[14:10]), .col21(EFO[19:15]), .col22(EFO[24:20]), .col23({5{1'b0}}), .col24(EGO[4:0]),
    .col25(EGO[9:5]), .col26(EGO[14:10]), .col27(EGO[19:15]), .col28(EGO[24:20]));

  // Other names for the same wires on the sheet: Power = in_1; Show = in_2
endmodule

module Interruptor (
  input  in_1,
  output out_2,
  output out_3
);

  not not_1 (out_3, in_1);

  assign out_2 = in_1;
endmodule
